// Logisim project 19101188_고은수_numberbaseball.circ as structural Verilog: 10 circuits, main circuit BCDcounter
module main (
  output out_1
);

  wire A0, A1, A2, B0, B1, B2, button_1_out, button_2_out, button_3_out, button_4_out, button_5_out,
       button_6_out, button_7_out, button_8_out, button_9_out, button_10_out, button_11_out, button_12_out,
       button_13_out, button_14_out, button_15_out, button_16_out, button_17_out, Check_out, First_out,
       RandomNum_out, Second_out, Third_out;
  wire [1:0] randomtest_1_out_6, randomtest_1_out_7, test_1_out_8, test_1_out_9, test_2_out_8, test_2_out_9;
  wire [3:0] bcdcounter_1_out_3, bcdcounter_1_out_4, bcdcounter_2_out_3, bcdcounter_2_out_4,
       bcdcounter_3_out_3, bcdcounter_3_out_4, bcdcounter_4_out_3, bcdcounter_4_out_4, bcdcounter_5_out_3,
       bcdcounter_5_out_4, bcdcounter_6_out_3, bcdcounter_6_out_4, bcdcounter_7_out_3, bcdcounter_7_out_4,
       bcdcounter_8_out_3, bcdcounter_8_out_4, bcdcounter_9_out_3, bcdcounter_9_out_4, bit_extender_1_out,
       bit_extender_2_out, bit_extender_3_out, bit_extender_4_out, bit_extender_5_out, bit_extender_6_out;
  wire [6:0] bcdcounter2_1_out_2, bcdcounter2_2_out_2, bcdcounter2_3_out_2;

  Button button_1 (.out(button_1_out));
  Button button_2 (.out(button_2_out));
  Button button_3 (.out(button_3_out));
  Button button_4 (.out(button_4_out));
  Button button_5 (.out(button_5_out));
  Button button_6 (.out(button_6_out));
  Button button_7 (.out(button_7_out));
  Button First (.out(First_out));
  Button button_8 (.out(button_8_out));
  Button Second (.out(Second_out));
  Button button_9 (.out(button_9_out));
  Button Third (.out(Third_out));
  Button button_10 (.out(button_10_out));
  Button Check (.out(Check_out));
  Button button_11 (.out(button_11_out));
  Button button_12 (.out(button_12_out));
  Button button_13 (.out(button_13_out));
  Button button_14 (.out(button_14_out));
  Button button_15 (.out(button_15_out));
  Button button_16 (.out(button_16_out));
  Button RandomNum (.out(RandomNum_out));
  Button button_17 (.out(button_17_out));
  BCDcounter bcdcounter_1 (
    .in_1(button_1_out), .in_2(button_2_out), .out_3(bcdcounter_1_out_3), .out_4(bcdcounter_1_out_4));
  BCDcounter bcdcounter_2 (
    .in_1(button_3_out), .in_2(button_4_out), .out_3(bcdcounter_2_out_3), .out_4(bcdcounter_2_out_4));
  BCDcounter bcdcounter_3 (
    .in_1(button_5_out), .in_2(button_6_out), .out_3(bcdcounter_3_out_3), .out_4(bcdcounter_3_out_4));
  BCDcounter2 bcdcounter2_1 (.in_1(button_7_out), .out_2(bcdcounter2_1_out_2));
  BCDcounter bcdcounter_4 (
    .in_1(First_out), .in_2(button_8_out), .out_3(bcdcounter_4_out_3), .out_4(bcdcounter_4_out_4));
  BCDcounter bcdcounter_5 (
    .in_1(Second_out), .in_2(button_9_out), .out_3(bcdcounter_5_out_3), .out_4(bcdcounter_5_out_4));
  BCDcounter bcdcounter_6 (
    .in_1(Third_out), .in_2(button_10_out), .out_3(bcdcounter_6_out_3), .out_4(bcdcounter_6_out_4));
  BCDcounter2 bcdcounter2_2 (.in_1(Check_out), .out_2(bcdcounter2_2_out_2));
  BCDcounter bcdcounter_7 (
    .in_1(button_11_out), .in_2(button_12_out), .out_3(bcdcounter_7_out_3), .out_4(bcdcounter_7_out_4));
  BCDcounter bcdcounter_8 (
    .in_1(button_13_out), .in_2(button_14_out), .out_3(bcdcounter_8_out_3), .out_4(bcdcounter_8_out_4));
  BCDcounter bcdcounter_9 (
    .in_1(button_15_out), .in_2(button_16_out), .out_3(bcdcounter_9_out_3), .out_4(bcdcounter_9_out_4));
  BCDcounter2 bcdcounter2_3 (.in_1(button_17_out), .out_2(bcdcounter2_3_out_2));
  Hex_Digit_Display hex_digit_display_1 (.value(bcdcounter_1_out_3));  // open: dp
  Hex_Digit_Display hex_digit_display_2 (.value(bcdcounter_2_out_3));  // open: dp
  Hex_Digit_Display hex_digit_display_3 (.value(bcdcounter_4_out_3));  // open: dp
  Hex_Digit_Display hex_digit_display_4 (.value(bcdcounter_5_out_3));  // open: dp
  Hex_Digit_Display hex_digit_display_5 (.value(bcdcounter_7_out_3));  // open: dp
  Hex_Digit_Display hex_digit_display_6 (.value(bcdcounter_8_out_3));  // open: dp
  Hex_Digit_Display hex_digit_display_7 (.value(bcdcounter_3_out_3));  // open: dp
  Hex_Digit_Display hex_digit_display_8 (.value(bcdcounter_6_out_3));  // open: dp
  Hex_Digit_Display hex_digit_display_9 (.value(bcdcounter_9_out_3));  // open: dp
  Button button_18 (.out(A0));
  Button button_19 (.out(A1));
  Button button_20 (.out(B0));
  Button button_21 (.out(B1));
  Button button_22 (.out(A2));
  Button button_23 (.out(B2));
  Hex_Digit_Display hex_digit_display_10 (.value(bit_extender_1_out));  // open: dp
  assign bit_extender_1_out = {{2{1'b0}}, test_1_out_8};  // Bit_Extender bit_extender_1
  test test_1 (
    .in_1(bcdcounter_1_out_4), .in_2(bcdcounter_2_out_4), .in_3(bcdcounter_3_out_4), .in_4(A0), .in_5(A1),
    .in_6(A2), .in_7(button_7_out), .out_8(test_1_out_8), .out_9(test_1_out_9));
  Hex_Digit_Display hex_digit_display_11 (.value(bit_extender_2_out));  // open: dp
  assign bit_extender_2_out = {{2{1'b0}}, test_2_out_8};  // Bit_Extender bit_extender_2
  test test_2 (
    .in_1(bcdcounter_4_out_4), .in_2(bcdcounter_5_out_4), .in_3(bcdcounter_6_out_4), .in_4(B0), .in_5(B1),
    .in_6(B2), .in_7(Check_out), .out_8(test_2_out_8), .out_9(test_2_out_9));
  Hex_Digit_Display hex_digit_display_12 (.value(bit_extender_3_out));  // open: dp
  assign bit_extender_3_out = {{2{1'b0}}, randomtest_1_out_6};  // Bit_Extender bit_extender_3
  randomTest randomtest_1 (
    .in_1(bcdcounter_7_out_4), .in_2(bcdcounter_8_out_4), .in_3(bcdcounter_9_out_4), .in_4(RandomNum_out),
    .in_5(button_17_out), .out_6(randomtest_1_out_6), .out_7(randomtest_1_out_7), .out_8(out_1));
  Hex_Digit_Display hex_digit_display_13 (.value(bit_extender_4_out));  // open: dp
  assign bit_extender_4_out = {{2{1'b0}}, test_1_out_9};  // Bit_Extender bit_extender_4
  Hex_Digit_Display hex_digit_display_14 (.value(bit_extender_5_out));  // open: dp
  assign bit_extender_5_out = {{2{1'b0}}, test_2_out_9};  // Bit_Extender bit_extender_5
  Hex_Digit_Display hex_digit_display_15 (.value(bit_extender_6_out));  // open: dp
  assign bit_extender_6_out = {{2{1'b0}}, randomtest_1_out_7};  // Bit_Extender bit_extender_6
  _7_Segment_Display u_7_segment_display_1 (
    .g(bcdcounter2_1_out_2[0]), .f(bcdcounter2_1_out_2[1]), .a(bcdcounter2_1_out_2[6]),
    .b(bcdcounter2_1_out_2[5]), .e(bcdcounter2_1_out_2[2]), .d(bcdcounter2_1_out_2[3]),
    .c(bcdcounter2_1_out_2[4]));  // open: dp
  _7_Segment_Display u_7_segment_display_2 (
    .g(bcdcounter2_2_out_2[0]), .f(bcdcounter2_2_out_2[1]), .a(bcdcounter2_2_out_2[6]),
    .b(bcdcounter2_2_out_2[5]), .e(bcdcounter2_2_out_2[2]), .d(bcdcounter2_2_out_2[3]),
    .c(bcdcounter2_2_out_2[4]));  // open: dp
  _7_Segment_Display u_7_segment_display_3 (
    .g(bcdcounter2_3_out_2[0]), .f(bcdcounter2_3_out_2[1]), .a(bcdcounter2_3_out_2[6]),
    .b(bcdcounter2_3_out_2[5]), .e(bcdcounter2_3_out_2[2]), .d(bcdcounter2_3_out_2[3]),
    .c(bcdcounter2_3_out_2[4]));  // open: dp

  // Notes on the sheet:
  //   First
  //   RESET
  //   Second
  //   RESET
  //   Third
  //   RESET
  //   Check
  //   RESET
  //   RESET
  //   RESET
  //   First
  //   RESET
  //   Second
  //   RESET
  //   Third
  //   RESET
  //   Check
  //   PLAYER 1
  //   PLAYER 2
  //   Prediction
  //   Prediction
  //   Prediction
  //   MULTI PLAY
  //   SINGLE PLAY
  //   Strike
  //   Strike
  //   Strike
  //   Ball
  //   Ball
  //   Ball
  //   19101188 KOEUNSOO
  //   Inning
  //   Inning
  //   Inning
endmodule

module BCDcounter (
  input  in_1,
  input  in_2,
  output [3:0] out_3,
  output [3:0] out_4
);

  wire and_1_out, or_1_out, or_2_out;

  J_K_Flip_Flop #(.trigger("falling")) j_k_ff_1 (
    .J(1'b1), .K(1'b1), .clk(in_1), .Q(out_3[0]), .reset(or_1_out));  // open: Qn, preset
  J_K_Flip_Flop #(.trigger("falling")) j_k_ff_2 (
    .J(1'b1), .K(1'b1), .clk(out_3[0]), .Q(out_3[1]), .reset(or_1_out));  // open: Qn, preset
  J_K_Flip_Flop #(.trigger("falling")) j_k_ff_3 (
    .J(1'b1), .K(1'b1), .clk(out_3[1]), .Q(out_3[2]), .reset(or_1_out));  // open: Qn, preset
  J_K_Flip_Flop #(.trigger("falling")) j_k_ff_4 (
    .J(1'b1), .K(1'b1), .clk(out_3[2]), .Q(out_3[3]), .reset(or_1_out));  // open: Qn, preset
  or or_1 (or_1_out, and_1_out, or_2_out);
  and and_1 (and_1_out, out_3[1], out_3[3]);
  or or_2 (or_2_out, 1'b0, in_2);

  assign out_4 = out_3;
endmodule

module BCDcounter2 (
  input  in_1,
  output [6:0] out_2
);

  wire and_1_out, or_1_out;
  wire [3:0] j_k_ff_1_q;

  J_K_Flip_Flop #(.trigger("falling")) j_k_ff_1 (
    .J(1'b1), .K(1'b1), .clk(in_1), .Q(j_k_ff_1_q[0]), .reset(or_1_out));  // open: Qn, preset
  J_K_Flip_Flop #(.trigger("falling")) j_k_ff_2 (
    .J(1'b1), .K(1'b1), .clk(j_k_ff_1_q[0]), .Q(j_k_ff_1_q[1]), .reset(or_1_out));  // open: Qn, preset
  J_K_Flip_Flop #(.trigger("falling")) j_k_ff_3 (
    .J(1'b1), .K(1'b1), .clk(j_k_ff_1_q[1]), .Q(j_k_ff_1_q[2]), .reset(or_1_out));  // open: Qn, preset
  J_K_Flip_Flop #(.trigger("falling")) j_k_ff_4 (
    .J(1'b1), .K(1'b1), .clk(j_k_ff_1_q[2]), .Q(j_k_ff_1_q[3]), .reset(or_1_out));  // open: Qn, preset
  or or_1 (or_1_out, and_1_out, 1'b0);
  // PlaRom #(.Contents("0 0 2 0 2 0*4 2 0 2 0 1 0 1 2 0*4 1 0*4 2 2 0 0 1 1 0 2 0 0 2 0*5 1 0*4 2 0 0 2 1 0 2 1 2 0 1 0 1 0 1 2 0*3 2 1 0 1 0 1 2 0*5 1 1 0 2 1 0 0 2 0 1 2 0*5 2 1 0 2 1 0 0 1 2 0 1 0*6 1 0*6 1 0*6 1 0*7 1 0*6 1 0*6 1 0*6 1 0*7 1 0*6 1 0*6 1 0*6 1 0*7 1 0*6 1 0*6 1 0*6 1 0*7 1 0*6 1 0*7 1 0*6 1 0*6 1 0*6 1 0*7 1 0*6 1 0*6 1 0*6 1"), .\and (26), .outputs(7)) plarom_1: pin names not known; wires that end beside it: j_k_ff_1_q, out_2
  and and_1 (and_1_out, j_k_ff_1_q[1], j_k_ff_1_q[3]);
  _7_Segment_Display u_7_segment_display_1 (
    .g(out_2[0]), .f(out_2[1]), .a(out_2[6]), .b(out_2[5]), .e(out_2[2]), .d(out_2[3]), .c(out_2[4]));  // open: dp

  // Notes on the sheet:
  //   Controller
endmodule

module saveNumber (
  input  in_1,
  input  in_2,
  input  in_3,
  output [3:0] out_4,
  output [3:0] out_5,
  output [3:0] out_6
);

  wire [3:0] bcdcounter_1_out_3, bcdcounter_2_out_3, bcdcounter_3_out_3;

  BCDcounter bcdcounter_1 (.in_1(in_1), .out_3(bcdcounter_1_out_3), .out_4(out_4));  // open: in_2
  BCDcounter bcdcounter_2 (.in_1(in_2), .out_3(bcdcounter_2_out_3), .out_4(out_5));  // open: in_2
  BCDcounter bcdcounter_3 (.in_1(in_3), .out_3(bcdcounter_3_out_3), .out_4(out_6));  // open: in_2
  Hex_Digit_Display hex_digit_display_1 (.value(bcdcounter_1_out_3));  // open: dp
  Hex_Digit_Display hex_digit_display_2 (.value(bcdcounter_2_out_3));  // open: dp
  Hex_Digit_Display hex_digit_display_3 (.value(bcdcounter_3_out_3));  // open: dp
endmodule

module test (
  input  [3:0] in_1,
  input  [3:0] in_2,
  input  [3:0] in_3,
  input  in_4,
  input  in_5,
  input  in_6,
  input  in_7,
  output [1:0] out_8,
  output [1:0] out_9
);

  wire Ball_c_out, Ball_s, comparator_10_eq, comparator_11_eq, comparator_12_eq, comparator_13_eq,
       comparator_14_eq, comparator_15_eq, comparator_16_eq, comparator_17_eq, comparator_18_eq, or_1_out,
       or_2_out, or_3_out, Strike_c_out, Strike_s;
  wire [2:0] comparator_1_eq, comparator_4_eq, comparator_7_eq;
  wire [3:0] savenumber_1_out_4, savenumber_1_out_5, savenumber_1_out_6;

  saveNumber savenumber_1 (
    .in_1(in_4), .in_2(in_5), .in_3(in_6), .out_4(savenumber_1_out_4), .out_5(savenumber_1_out_5),
    .out_6(savenumber_1_out_6));
  Comparator #(.width(4)) comparator_1 (.a(savenumber_1_out_4), .b(in_1), .eq(comparator_1_eq[0]));  // open: gt, lt
  Comparator #(.width(4)) comparator_2 (.a(savenumber_1_out_4), .b(in_2), .eq(comparator_1_eq[1]));  // open: gt, lt
  Comparator #(.width(4)) comparator_3 (.a(savenumber_1_out_4), .b(in_3), .eq(comparator_1_eq[2]));  // open: gt, lt
  Comparator #(.width(4)) comparator_4 (.a(savenumber_1_out_5), .b(in_1), .eq(comparator_4_eq[0]));  // open: gt, lt
  Comparator #(.width(4)) comparator_5 (.a(savenumber_1_out_5), .b(in_2), .eq(comparator_4_eq[1]));  // open: gt, lt
  Comparator #(.width(4)) comparator_6 (.a(savenumber_1_out_5), .b(in_3), .eq(comparator_4_eq[2]));  // open: gt, lt
  Comparator #(.width(4)) comparator_7 (.a(savenumber_1_out_6), .b(in_1), .eq(comparator_7_eq[0]));  // open: gt, lt
  Comparator #(.width(4)) comparator_8 (.a(savenumber_1_out_6), .b(in_2), .eq(comparator_7_eq[1]));  // open: gt, lt
  Comparator #(.width(4)) comparator_9 (.a(savenumber_1_out_6), .b(in_3), .eq(comparator_7_eq[2]));  // open: gt, lt
  Comparator #(.width(3)) comparator_10 (.a(comparator_1_eq), .b(3'b001), .eq(comparator_10_eq));  // open: gt, lt
  Comparator #(.width(3)) comparator_11 (.a(comparator_1_eq), .b(3'b010), .eq(comparator_11_eq));  // open: gt, lt
  Comparator #(.width(3)) comparator_12 (.a(comparator_1_eq), .b(3'b100), .eq(comparator_12_eq));  // open: gt, lt
  Comparator #(.width(3)) comparator_13 (.a(comparator_4_eq), .b(3'b001), .eq(comparator_13_eq));  // open: gt, lt
  Comparator #(.width(3)) comparator_14 (.a(comparator_4_eq), .b(3'b010), .eq(comparator_14_eq));  // open: gt, lt
  Comparator #(.width(3)) comparator_15 (.a(comparator_4_eq), .b(3'b100), .eq(comparator_15_eq));  // open: gt, lt
  Comparator #(.width(3)) comparator_16 (.a(comparator_7_eq), .b(3'b001), .eq(comparator_16_eq));  // open: gt, lt
  Comparator #(.width(3)) comparator_17 (.a(comparator_7_eq), .b(3'b010), .eq(comparator_17_eq));  // open: gt, lt
  Comparator #(.width(3)) comparator_18 (.a(comparator_7_eq), .b(3'b100), .eq(comparator_18_eq));  // open: gt, lt
  or or_1 (or_1_out, comparator_11_eq, comparator_12_eq);
  or or_2 (or_2_out, comparator_16_eq, comparator_17_eq);
  or or_3 (or_3_out, comparator_13_eq, comparator_15_eq);
  fullAdder Strike (
    .A(comparator_10_eq), .B(comparator_14_eq), .C_in(comparator_18_eq), .S(Strike_s), .C_out(Strike_c_out));
  fullAdder Ball (.A(or_1_out), .B(or_3_out), .C_in(or_2_out), .S(Ball_s), .C_out(Ball_c_out));
  and and_1 (out_8[0], in_7, Strike_s);
  and and_2 (out_8[1], Strike_c_out, in_7);
  and and_3 (out_9[0], in_7, Ball_s);
  and and_4 (out_9[1], Ball_c_out, in_7);
endmodule

module halfAdder (
  input  A,
  input  B,
  output S,
  output C
);

  xor xor_1 (S, A, B);
  and and_1 (C, A, B);
endmodule

module fullAdder (
  input  A,
  input  B,
  input  C_in,
  output S,
  output C_out
);

  wire halfadder_1_c, halfadder_1_s, halfadder_2_c;

  halfAdder halfadder_1 (.A(A), .B(B), .S(halfadder_1_s), .C(halfadder_1_c));
  halfAdder halfadder_2 (.A(halfadder_1_s), .B(C_in), .S(S), .C(halfadder_2_c));
  or or_1 (C_out, halfadder_1_c, halfadder_2_c);
endmodule

module Inning (
  input  [3:0] in_1,
  output [6:0] out_2
);

  // PlaRom #(.Contents("0 0 2 0 2 0*4 2 0 2 0 1 0 1 2 0*4 1 0*4 2 2 0 0 1 1 0 2 0 0 2 0*5 1 0*4 2 0 0 2 1 0 2 1 2 0 1 0 1 0 1 2 0*3 2 1 0 1 0 1 2 0*5 1 1 0 2 1 0 0 2 0 1 2 0*5 2 1 0 2 1 0 0 1 2 0 1 0*6 1 0*6 1 0*6 1 0*7 1 0*6 1 0*6 1 0*6 1 0*7 1 0*6 1 0*6 1 0*6 1 0*7 1 0*6 1 0*6 1 0*6 1 0*7 1 0*6 1 0*7 1 0*6 1 0*6 1 0*6 1 0*7 1 0*6 1 0*6 1 0*6 1"), .\and (26), .outputs(7)) plarom_1: pin names not known; wires that end beside it: in_1, out_2
  _7_Segment_Display u_7_segment_display_1 (
    .g(out_2[0]), .f(out_2[1]), .a(out_2[6]), .b(out_2[5]), .e(out_2[2]), .d(out_2[3]), .c(out_2[4]));  // open: dp

  // Notes on the sheet:
  //   Controller
endmodule

module randomNum (
  input  in_1,
  output [3:0] out_2,
  output [3:0] out_3,
  output [3:0] out_4,
  output out_5
);

  wire ab, bc, ca, clock_1_out, clock_2_out, clock_3_out, comparator_2_gt, comparator_5_gt, comparator_6_gt,
       multiplexer_1_out, multiplexer_2_out, multiplexer_3_out, or_1_out, or_2_out, or_3_out;

  Clock clock_1 (.out(clock_1_out));
  Random #(.width(4)) random_1 (.clk(multiplexer_1_out), .out(out_2));  // open: clr, next
  Multiplexer multiplexer_1 (.in0(in_1), .in1(clock_1_out), .out(multiplexer_1_out), .sel(or_1_out));
  or or_1 (or_1_out, ab, comparator_2_gt);
  Comparator #(.mode("unsigned"), .width(4)) comparator_1 (.a(out_2), .b(out_3), .eq(ab));  // open: gt, lt
  Comparator #(.mode("unsigned"), .width(4)) comparator_2 (
    .a(out_2), .b(4'b1001), .gt(comparator_2_gt));  // open: eq, lt
  Comparator #(.mode("unsigned"), .width(4)) comparator_3 (.a(out_3), .b(out_4), .eq(bc));  // open: gt, lt
  Random #(.seed(200), .width(4)) random_2 (.clk(multiplexer_2_out), .out(out_3));  // open: clr, next
  Multiplexer multiplexer_2 (.in0(in_1), .in1(clock_2_out), .out(multiplexer_2_out), .sel(or_2_out));
  Clock clock_2 (.out(clock_2_out));
  or or_2 (or_2_out, bc, comparator_5_gt);
  nor ready (out_5, comparator_2_gt, comparator_5_gt, comparator_6_gt);
  Comparator #(.mode("unsigned"), .width(4)) comparator_4 (.a(out_2), .b(out_4), .eq(ca));  // open: gt, lt
  Comparator #(.mode("unsigned"), .width(4)) comparator_5 (
    .a(out_3), .b(4'b1001), .gt(comparator_5_gt));  // open: eq, lt
  Multiplexer multiplexer_3 (.in0(in_1), .in1(clock_3_out), .out(multiplexer_3_out), .sel(or_3_out));
  Clock clock_3 (.out(clock_3_out));
  or or_3 (or_3_out, ca, comparator_6_gt);
  Random #(.seed(400), .width(4)) random_3 (.clk(multiplexer_3_out), .out(out_4));  // open: clr, next
  Comparator #(.mode("unsigned"), .width(4)) comparator_6 (
    .a(out_4), .b(4'b1001), .gt(comparator_6_gt));  // open: eq, lt

  // Other names for the same wires on the sheet: a[3:0] = out_2; b[3:0] = out_3; c[3:0] = out_4
endmodule

module randomTest (
  input  [3:0] in_1,
  input  [3:0] in_2,
  input  [3:0] in_3,
  input  in_4,
  input  in_5,
  output [1:0] out_6,
  output [1:0] out_7,
  output out_8
);

  wire Ball_c_out, Ball_s, comparator_10_eq, comparator_11_eq, comparator_12_eq, comparator_13_eq,
       comparator_14_eq, comparator_15_eq, comparator_16_eq, comparator_17_eq, comparator_18_eq, or_1_out,
       or_2_out, or_3_out, Strike_c_out, Strike_s;
  wire [2:0] comparator_1_eq, comparator_4_eq, comparator_7_eq;
  wire [3:0] randomnum_1_out_2, randomnum_1_out_3, randomnum_1_out_4;

  randomNum randomnum_1 (
    .in_1(in_4), .out_2(randomnum_1_out_2), .out_3(randomnum_1_out_3), .out_4(randomnum_1_out_4),
    .out_5(out_8));
  Comparator #(.width(4)) comparator_1 (.a(randomnum_1_out_2), .b(in_1), .eq(comparator_1_eq[0]));  // open: gt, lt
  Comparator #(.width(4)) comparator_2 (.a(randomnum_1_out_2), .b(in_2), .eq(comparator_1_eq[1]));  // open: gt, lt
  Comparator #(.width(4)) comparator_3 (.a(randomnum_1_out_2), .b(in_3), .eq(comparator_1_eq[2]));  // open: gt, lt
  Comparator #(.width(4)) comparator_4 (.a(randomnum_1_out_3), .b(in_1), .eq(comparator_4_eq[0]));  // open: gt, lt
  Comparator #(.width(4)) comparator_5 (.a(randomnum_1_out_3), .b(in_2), .eq(comparator_4_eq[1]));  // open: gt, lt
  Comparator #(.width(4)) comparator_6 (.a(randomnum_1_out_3), .b(in_3), .eq(comparator_4_eq[2]));  // open: gt, lt
  Comparator #(.width(4)) comparator_7 (.a(randomnum_1_out_4), .b(in_1), .eq(comparator_7_eq[0]));  // open: gt, lt
  Comparator #(.width(4)) comparator_8 (.a(randomnum_1_out_4), .b(in_2), .eq(comparator_7_eq[1]));  // open: gt, lt
  Comparator #(.width(4)) comparator_9 (.a(randomnum_1_out_4), .b(in_3), .eq(comparator_7_eq[2]));  // open: gt, lt
  Comparator #(.width(3)) comparator_10 (.a(comparator_1_eq), .b(3'b001), .eq(comparator_10_eq));  // open: gt, lt
  Comparator #(.width(3)) comparator_11 (.a(comparator_1_eq), .b(3'b010), .eq(comparator_11_eq));  // open: gt, lt
  Comparator #(.width(3)) comparator_12 (.a(comparator_1_eq), .b(3'b100), .eq(comparator_12_eq));  // open: gt, lt
  Comparator #(.width(3)) comparator_13 (.a(comparator_4_eq), .b(3'b001), .eq(comparator_13_eq));  // open: gt, lt
  Comparator #(.width(3)) comparator_14 (.a(comparator_4_eq), .b(3'b010), .eq(comparator_14_eq));  // open: gt, lt
  Comparator #(.width(3)) comparator_15 (.a(comparator_4_eq), .b(3'b100), .eq(comparator_15_eq));  // open: gt, lt
  Comparator #(.width(3)) comparator_16 (.a(comparator_7_eq), .b(3'b001), .eq(comparator_16_eq));  // open: gt, lt
  Comparator #(.width(3)) comparator_17 (.a(comparator_7_eq), .b(3'b010), .eq(comparator_17_eq));  // open: gt, lt
  Comparator #(.width(3)) comparator_18 (.a(comparator_7_eq), .b(3'b100), .eq(comparator_18_eq));  // open: gt, lt
  or or_1 (or_1_out, comparator_11_eq, comparator_12_eq);
  or or_2 (or_2_out, comparator_16_eq, comparator_17_eq);
  or or_3 (or_3_out, comparator_13_eq, comparator_15_eq);
  fullAdder Strike (
    .A(comparator_10_eq), .B(comparator_14_eq), .C_in(comparator_18_eq), .S(Strike_s), .C_out(Strike_c_out));
  fullAdder Ball (.A(or_1_out), .B(or_3_out), .C_in(or_2_out), .S(Ball_s), .C_out(Ball_c_out));
  and and_1 (out_6[0], in_5, Strike_s);
  and and_2 (out_6[1], Strike_c_out, in_5);
  and and_3 (out_7[0], in_5, Ball_s);
  and and_4 (out_7[1], Ball_c_out, in_5);
endmodule
